// Logisim project compounder.circ as structural Verilog: 4 circuits, main circuit main
module main (
);

  wire converter_1_sign, linear_to_fp_1_fifth, undriven;
  wire [2:0] linear_to_fp_1_exp, linear_to_fp_1_sig, rounding_1_e;
  wire [4:0] rounding_1_f;
  wire [11:0] converter_1_mag;

  Converter converter_1 (.d_in_11(undriven), .sign(converter_1_sign), .mag(converter_1_mag));
  Linear_to_FP linear_to_fp_1 (
    .d_in_4_2(converter_1_mag), .sig(linear_to_fp_1_sig), .exp(linear_to_fp_1_exp),
    .fifth(linear_to_fp_1_fifth));
  Rounding rounding_1 (
    .in_1(linear_to_fp_1_sig), .in_2(linear_to_fp_1_exp), .in_3(linear_to_fp_1_fifth), .E(rounding_1_e),
    .F(rounding_1_f));

  // Notes on the sheet:
  //   D
  //   converter
  //   S
  //   linear_to_FP
  //   rounding
  //   E
  //   F
endmodule

module Converter (
  input  d_in_11,
  output sign,
  output [11:0] mag
);

  wire comparator_1_eq, undriven_3;
  wire [11:0] adder_1_out, multiplexer_1_out, not_1_out, not_2_out, undriven, undriven_2;

  assign not_1_out = ~undriven;  // NOT_Gate not_1, 12 bits wide
  Adder #(.width(12)) adder_1 (.a(12'h1), .b(not_1_out), .out(adder_1_out));  // open: cin, cout
  Multiplexer #(.width(12), .enable("false")) multiplexer_1 (
    .in0(adder_1_out), .in1(undriven_2), .out(multiplexer_1_out), .sel(undriven_3));
  assign not_2_out = ~multiplexer_1_out;  // NOT_Gate not_2, 12 bits wide
  Comparator #(.width(12)) comparator_1 (.a(12'h800), .b(multiplexer_1_out), .eq(comparator_1_eq));  // open: gt, lt
  Multiplexer #(.width(12), .enable("false")) multiplexer_2 (
    .in0(not_2_out), .in1(multiplexer_1_out), .out(mag), .sel(comparator_1_eq));

  assign sign = d_in_11;

  // Notes on the sheet:
  //   d_in[11:0]
  //   d_in[11:0]
  //   d_in[11]
endmodule

module Linear_to_FP (
  input  [11:0] d_in_4_2,
  output [2:0] sig,
  output [2:0] exp,
  output fifth
);

  wire multiplexer_3_out, or_1_out, priority_encoder_1_en_out, undriven, undriven_2, undriven_3, undriven_6,
       undriven_7, undriven_8, undriven_9, undriven_10, undriven_13, undriven_19, undriven_20, undriven_21,
       undriven_22, undriven_23, undriven_24, undriven_25, undriven_26, undriven_27;
  wire [2:0] multiplexer_1_out, undriven_4, undriven_5, undriven_11, undriven_12, undriven_14, undriven_15,
       undriven_16, undriven_17, undriven_18;

  or or_1 (or_1_out, undriven, undriven_2);
  Multiplexer #(.width(3), .enable("false")) multiplexer_1 (
    .in0(undriven_4), .in1(undriven_5), .out(multiplexer_1_out), .sel(undriven_13));
  Priority_Encoder priority_encoder_1 (
    .in0(1'b1), .in1(undriven_8), .in2(undriven_6), .in3(undriven_3), .in4(undriven_7), .in5(undriven_9),
    .in6(undriven_10), .in7(or_1_out), .out(exp), .en_in(1'b1), .en_out(priority_encoder_1_en_out));  // open: gs
  Multiplexer #(.select(3), .width(3), .enable("false")) multiplexer_2 (
    .in0(undriven_18), .in1(undriven_17), .in2(undriven_16), .in3(undriven_15), .in4(undriven_14),
    .in5(undriven_11), .in6(undriven_12), .in7(multiplexer_1_out), .out(sig), .sel(exp));
  Multiplexer #(.enable("false")) multiplexer_3 (
    .in0(undriven_19), .in1(undriven_20), .out(multiplexer_3_out), .sel(undriven_23));
  Multiplexer #(.select(3), .enable("false")) multiplexer_4 (
    .in0(1'b0), .in1(undriven_27), .in2(undriven_26), .in3(undriven_25), .in4(undriven_24),
    .in5(undriven_21), .in6(undriven_22), .in7(multiplexer_3_out), .out(fifth), .sel(exp));
  // also tied to VCC on the sheet: priority_encoder_1_en_out

  // Notes on the sheet:
  //   d_in[10:7]
  //   d_in[11:8]
  //   d_in[6]
  //   d_in[7]
  //   d_in[8]
  //   d_in[9]
  //   d_in[10]
  //   d_in[11]
  //   d_in[5:2]
  //   d_in[6:3]
  //   d_in[7:4]
  //   d_in[8:5]
  //   d_in[9:6]
  //   d_in[11]
  //   d_in[4]
  //   d_in[5]
  //   d_in[3:0]
  //   d_in[4]
  //   d_in[5]
  //   d_in[6]
  //   d_in[7]
  //   d_in[11]
  //   d_in[0]
  //   d_in[1]
  //   d_in[2]
  //   d_in[3]
endmodule

module Rounding (
  input  [2:0] in_1,
  input  [2:0] in_2,
  input  in_3,
  output [2:0] E,
  output [4:0] F
);

  wire and_1_out, and_2_out, comparator_1_eq, comparator_2_eq, comparator_3_eq, comparator_4_eq,
       comparator_5_eq, comparator_6_eq, undriven_5, undriven_7, undriven_8, undriven_11;
  wire [2:0] adder_1_out, multiplexer_1_out, undriven, undriven_2, undriven_9, undriven_10;
  wire [3:0] undriven_4, undriven_12;
  wire [4:0] adder_2_out, multiplexer_2_out, multiplexer_4_out, multiplexer_5_out, shifter_1_out, undriven_3,
       undriven_6;

  Adder #(.width(3)) adder_1 (.a(undriven), .b(3'b001), .out(adder_1_out), .cin(undriven_5));  // open: cout
  Comparator #(.width(3)) comparator_1 (.a(undriven_2), .b(3'b111), .eq(comparator_1_eq));  // open: gt, lt
  Comparator #(.width(4)) comparator_2 (.a(4'b1111), .b(undriven_4), .eq(comparator_2_eq));  // open: gt, lt
  Adder #(.width(5)) adder_2 (.a(undriven_3), .b(5'b00001), .out(adder_2_out));  // open: cin, cout
  Multiplexer #(.width(3), .enable("false")) multiplexer_1 (
    .in0(adder_1_out), .in1(adder_1_out), .out(multiplexer_1_out), .sel(comparator_1_eq));
  and and_1 (and_1_out, undriven_7, comparator_2_eq);
  Multiplexer #(.width(5), .enable("false")) multiplexer_2 (
    .in0(undriven_6), .in1(adder_2_out), .out(multiplexer_2_out), .sel(undriven_8));
  Multiplexer #(.width(3), .enable("false")) multiplexer_3 (
    .in0(multiplexer_1_out), .in1(undriven_9), .out(E), .sel(and_1_out));
  Multiplexer #(.width(5), .enable("false")) multiplexer_4 (
    .in0(multiplexer_2_out), .in1(shifter_1_out), .out(multiplexer_4_out), .sel(comparator_3_eq));
  Shifter #(.width(5), .shift("lr")) shifter_1 (.in(multiplexer_2_out), .\dist (3'b001), .out(shifter_1_out));
  Comparator #(.width(5)) comparator_3 (.a(multiplexer_2_out), .b(5'b10000), .eq(comparator_3_eq));  // open: gt, lt
  Multiplexer #(.width(5), .enable("false")) multiplexer_5 (
    .in0(multiplexer_2_out), .in1(multiplexer_4_out), .out(multiplexer_5_out));  // open: sel
  and and_2 (and_2_out, comparator_4_eq, comparator_5_eq, comparator_6_eq);
  Comparator #(.width(1)) comparator_4 (.a(undriven_11), .b(1'b1), .eq(comparator_4_eq));  // open: gt, lt
  Comparator #(.width(4)) comparator_5 (.a(undriven_12), .b(4'b1111), .eq(comparator_5_eq));  // open: gt, lt
  Comparator #(.width(3)) comparator_6 (.a(undriven_10), .b(3'b111), .eq(comparator_6_eq));  // open: gt, lt
  Multiplexer #(.width(5), .enable("false")) multiplexer_6 (
    .in0(multiplexer_5_out), .out(F), .sel(and_2_out));  // open: in1

  // Notes on the sheet:
  //   exp
  //   exp
  //   sig
  //   sig
  //   exp
  //   fifth
  //   sig
  //   exp
  //   fifth
  //   fifth
  //   fifth
  //   sig
  //   exp
endmodule
