// Logisim project converter.circ as structural Verilog: 1 circuit, main circuit main
module main (
);

  wire comparator_1_eq, undriven_3;
  wire [11:0] adder_1_out, multiplexer_1_out, multiplexer_2_out, not_1_out, not_2_out, undriven, undriven_2;

  assign not_1_out = ~undriven;  // NOT_Gate not_1, 12 bits wide
  Adder #(.width(12)) adder_1 (.a(12'h1), .b(not_1_out), .out(adder_1_out));  // open: cin, cout
  Multiplexer #(.width(12), .enable("false")) multiplexer_1 (
    .in0(adder_1_out), .in1(undriven_2), .out(multiplexer_1_out), .sel(undriven_3));
  assign not_2_out = ~multiplexer_1_out;  // NOT_Gate not_2, 12 bits wide
  Comparator #(.width(12)) comparator_1 (.a(12'h800), .b(multiplexer_1_out), .eq(comparator_1_eq));  // open: gt, lt
  Multiplexer #(.width(12), .enable("false")) multiplexer_2 (
    .in0(not_2_out), .in1(multiplexer_1_out), .out(multiplexer_2_out), .sel(comparator_1_eq));

  // Notes on the sheet:
  //   d_in[11:0]
  //   d_in[11:0]
  //   d_in[11]
  //   d_in[11]
  //   sign
  //   mag
endmodule
