// Logisim project linear_to_fp.circ as structural Verilog: 1 circuit, main circuit main
module main (
);

  wire multiplexer_3_out, multiplexer_4_out, or_1_out, priority_encoder_1_en_out, undriven, undriven_2,
       undriven_3, undriven_6, undriven_7, undriven_8, undriven_9, undriven_10, undriven_13, undriven_19,
       undriven_20, undriven_21, undriven_22, undriven_23, undriven_24, undriven_25, undriven_26, undriven_27;
  wire [2:0] multiplexer_1_out, multiplexer_2_out, priority_encoder_1_out, undriven_4, undriven_5,
       undriven_11, undriven_12, undriven_14, undriven_15, undriven_16, undriven_17, undriven_18;

  or or_1 (or_1_out, undriven, undriven_2);
  Multiplexer #(.width(3), .enable("false")) multiplexer_1 (
    .in0(undriven_4), .in1(undriven_5), .out(multiplexer_1_out), .sel(undriven_13));
  Priority_Encoder priority_encoder_1 (
    .in0(1'b1), .in1(undriven_8), .in2(undriven_6), .in3(undriven_3), .in4(undriven_7), .in5(undriven_9),
    .in6(undriven_10), .in7(or_1_out), .out(priority_encoder_1_out), .en_in(1'b1),
    .en_out(priority_encoder_1_en_out));  // open: gs
  Multiplexer #(.select(3), .width(3), .enable("false")) multiplexer_2 (
    .in0(undriven_18), .in1(undriven_17), .in2(undriven_16), .in3(undriven_15), .in4(undriven_14),
    .in5(undriven_11), .in6(undriven_12), .in7(multiplexer_1_out), .out(multiplexer_2_out),
    .sel(priority_encoder_1_out));
  Multiplexer #(.enable("false")) multiplexer_3 (
    .in0(undriven_19), .in1(undriven_20), .out(multiplexer_3_out), .sel(undriven_23));
  Multiplexer #(.select(3), .enable("false")) multiplexer_4 (
    .in0(1'b0), .in1(undriven_27), .in2(undriven_26), .in3(undriven_25), .in4(undriven_24),
    .in5(undriven_21), .in6(undriven_22), .in7(multiplexer_3_out), .out(multiplexer_4_out),
    .sel(priority_encoder_1_out));
  // also tied to VCC on the sheet: priority_encoder_1_en_out

  // Notes on the sheet:
  //   d_in[10:7]
  //   d_in[11:8]
  //   d_in[6]
  //   d_in[7]
  //   d_in[8]
  //   d_in[9]
  //   d_in[10]
  //   d_in[11]
  //   d_in[4:2]
  //   d_in[5:2]
  //   d_in[6:3]
  //   d_in[7:4]
  //   d_in[8:5]
  //   d_in[9:6]
  //   d_in[11]
  //   d_in[4]
  //   d_in[5]
  //   d_in[3:0]
  //   d_in[4]
  //   d_in[5]
  //   d_in[6]
  //   d_in[7]
  //   d_in[11]
  //   exp
  //   d_in[0]
  //   d_in[1]
  //   d_in[2]
  //   d_in[3]
  //   sig
  //   fifth
endmodule
