// Logisim project rounding.circ as structural Verilog: 1 circuit, main circuit main
module main (
);

  wire and_1_out, and_2_out, comparator_1_eq, comparator_2_eq, comparator_3_eq, comparator_4_eq,
       comparator_5_eq, comparator_6_eq, undriven_5, undriven_7, undriven_8, undriven_11;
  wire [2:0] adder_1_out, multiplexer_1_out, multiplexer_3_out, undriven, undriven_2, undriven_9, undriven_10;
  wire [3:0] undriven_4, undriven_12;
  wire [4:0] adder_2_out, multiplexer_2_out, multiplexer_4_out, multiplexer_5_out, multiplexer_6_out,
       shifter_1_out, undriven_3, undriven_6;

  Adder #(.width(3)) adder_1 (.a(undriven), .b(3'b001), .out(adder_1_out), .cin(undriven_5));  // open: cout
  Comparator #(.width(3)) comparator_1 (.a(undriven_2), .b(3'b111), .eq(comparator_1_eq));  // open: gt, lt
  Comparator #(.width(4)) comparator_2 (.a(4'b1111), .b(undriven_4), .eq(comparator_2_eq));  // open: gt, lt
  Adder #(.width(5)) adder_2 (.a(undriven_3), .b(5'b00001), .out(adder_2_out));  // open: cin, cout
  Multiplexer #(.width(3), .enable("false")) multiplexer_1 (
    .in0(adder_1_out), .in1(adder_1_out), .out(multiplexer_1_out), .sel(comparator_1_eq));
  and and_1 (and_1_out, undriven_7, comparator_2_eq);
  Multiplexer #(.width(5), .enable("false")) multiplexer_2 (
    .in0(undriven_6), .in1(adder_2_out), .out(multiplexer_2_out), .sel(undriven_8));
  Multiplexer #(.width(3), .enable("false")) multiplexer_3 (
    .in0(multiplexer_1_out), .in1(undriven_9), .out(multiplexer_3_out), .sel(and_1_out));
  Multiplexer #(.width(5), .enable("false")) multiplexer_4 (
    .in0(multiplexer_2_out), .in1(shifter_1_out), .out(multiplexer_4_out), .sel(comparator_3_eq));
  Shifter #(.width(5), .shift("lr")) shifter_1 (.in(multiplexer_2_out), .\dist (3'b001), .out(shifter_1_out));
  Comparator #(.width(5)) comparator_3 (.a(multiplexer_2_out), .b(5'b10000), .eq(comparator_3_eq));  // open: gt, lt
  Multiplexer #(.width(5), .enable("false")) multiplexer_5 (
    .in0(multiplexer_2_out), .in1(multiplexer_4_out), .out(multiplexer_5_out));  // open: sel
  and and_2 (and_2_out, comparator_4_eq, comparator_5_eq, comparator_6_eq);
  Comparator #(.width(1)) comparator_4 (.a(undriven_11), .b(1'b1), .eq(comparator_4_eq));  // open: gt, lt
  Comparator #(.width(4)) comparator_5 (.a(undriven_12), .b(4'b1111), .eq(comparator_5_eq));  // open: gt, lt
  Comparator #(.width(3)) comparator_6 (.a(undriven_10), .b(3'b111), .eq(comparator_6_eq));  // open: gt, lt
  Multiplexer #(.width(5), .enable("false")) multiplexer_6 (
    .in0(multiplexer_5_out), .out(multiplexer_6_out), .sel(and_2_out));  // open: in1

  // Notes on the sheet:
  //   exp
  //   exp
  //   sig
  //   sig
  //   exp
  //   fifth
  //   sig
  //   exp
  //   fifth
  //   E
  //   fifth
  //   fifth
  //   sig
  //   exp
  //   F
endmodule
