// Logisim project debouncer.circ as structural Verilog: 1 circuit, main circuit main
module main (
);

  wire button_state_reg_q, button_sync_0_q, clock_1_out, comparator_1_eq, multiplexer_2_out,
       multiplexer_3_out, not_1_out, undriven;
  wire [1:0] adder_1_out, btn_cnt_q, multiplexer_1_out;

  Clock clock_1 (.out(clock_1_out));
  Adder #(.width(2)) adder_1 (.a(btn_cnt_q), .b(2'b01), .out(adder_1_out));  // open: cin, cout
  Register #(.width(1)) button_sync_0 (.D(undriven), .en(clock_1_out), .Q(button_sync_0_q));  // open: clk, clr
  Multiplexer #(.width(2), .enable("false")) multiplexer_1 (
    .in0(adder_1_out), .in1(2'b00), .out(multiplexer_1_out), .sel(button_sync_0_q));
  Comparator #(.width(2)) comparator_1 (
    .a(btn_cnt_q), .b(2'b11), .eq(comparator_1_eq), .lt(comparator_1_eq));  // open: gt
  Register #(.width(2)) btn_cnt (.D(multiplexer_1_out), .en(clock_1_out), .Q(btn_cnt_q));  // open: clk, clr
  not not_1 (not_1_out, button_state_reg_q);
  Multiplexer #(.enable("false")) multiplexer_2 (
    .in0(multiplexer_3_out), .in1(1'b1), .out(multiplexer_2_out), .sel(button_sync_0_q));
  Multiplexer #(.enable("false")) multiplexer_3 (
    .in0(button_state_reg_q), .in1(not_1_out), .out(multiplexer_3_out), .sel(comparator_1_eq));
  Register #(.width(1)) button_state_reg (
    .D(multiplexer_2_out), .en(clock_1_out), .Q(button_state_reg_q));  // open: clk, clr

  // Notes on the sheet:
  //   button
  //   button_state
endmodule
