// Logisim project disiplayTime.circ as structural Verilog: 1 circuit, main circuit main
module main (
);

  wire [3:0] undriven;
  wire [7:0] multiplexer_1_out;

  Multiplexer #(.select(4), .width(8), .enable("false")) multiplexer_1 (
    .in0(8'hc0), .in1(8'hf9), .in2(8'ha4), .in3(8'hb0), .in4(8'h99), .in5(8'h92), .in6(8'h82), .in7(8'hf8),
    .in8(8'h80), .in9(8'h90), .in10(8'hc0), .in11(8'hc0), .in12(8'hc0), .in13(8'hc0), .in14(8'hc0),
    .in15(8'hc0), .out(multiplexer_1_out), .sel(undriven));

  // Notes on the sheet:
  //   digit[3:0]
  //   seg[7:0]
endmodule
