// Logisim project stopwatch.circ as structural Verilog: 5 circuits, main circuit main
module main (
);

  wire clock_1_out, clock_2_out_3, clock_2_out_4, clock_2_out_5, clock_2_out_6, comparator_1_eq,
       comparator_1_gt, comparator_1_lt, debouncer_2_out_3, or_1_out, or_2_out, undriven, undriven_2,
       undriven_3, undriven_4, undriven_5;
  wire [1:0] adder_1_out, cnt_q;
  wire [3:0] counter_1_out_8, counter_1_out_9, counter_1_out_10, counter_1_out_11, multiplexer_2_out;
  wire [7:0] displaytime_1_out_2, displaytime_2_out_2, displaytime_3_out_2, displaytime_4_out_2,
       multiplexer_1_out, multiplexer_3_out, multiplexer_4_out, multiplexer_5_out, multiplexer_6_out;

  Clock_part clock_1 (.out(clock_1_out));
  Adder #(.width(2)) adder_1 (.a(cnt_q), .b(2'b01), .out(adder_1_out));  // open: cin, cout
  Debouncer debouncer_1 (.in_1(clock_1_out), .in_2(clock_1_out));  // open: out_3
  Clock clock_2 (
    .in_1(clock_1_out), .in_2(clock_1_out), .out_3(clock_2_out_3), .out_4(clock_2_out_4),
    .out_5(clock_2_out_5), .out_6(clock_2_out_6));
  Register #(.width(2)) cnt (.D(adder_1_out), .en(clock_2_out_5), .Q(cnt_q));  // open: clk, clr
  Multiplexer #(.select(2), .width(8), .enable("false")) multiplexer_1 (
    .in0(displaytime_4_out_2), .in1(displaytime_3_out_2), .in2(displaytime_2_out_2),
    .in3(displaytime_1_out_2), .out(multiplexer_1_out), .sel(cnt_q));
  Debouncer debouncer_2 (.in_1(clock_2_out_5), .in_2(undriven), .out_3(debouncer_2_out_3));
  Comparator #(.width(2)) comparator_1 (
    .a(cnt_q), .b(2'b10), .gt(comparator_1_gt), .eq(comparator_1_eq), .lt(comparator_1_lt));
  or or_1 (or_1_out, comparator_1_eq, comparator_1_lt);
  Counter counter_1 (
    .in_1(clock_1_out), .in_2(clock_2_out_3), .in_3(clock_2_out_4), .in_4(clock_1_out),
    .in_5(debouncer_2_out_3), .in_6(undriven_2), .in_7(undriven_3), .out_8(counter_1_out_8),
    .out_9(counter_1_out_9), .out_10(counter_1_out_10), .out_11(counter_1_out_11));
  displayTime displaytime_1 (.in_1(counter_1_out_11), .out_2(displaytime_1_out_2));
  or or_2 (or_2_out, clock_2_out_6, or_1_out);
  Multiplexer #(.select(2), .width(4), .enable("false")) multiplexer_2 (
    .in0(4'b1110), .in1(4'b1101), .in2(4'b1011), .in3(4'b0111), .out(multiplexer_2_out), .sel(cnt_q));
  Multiplexer #(.width(8), .enable("false")) multiplexer_3 (
    .in0(multiplexer_1_out), .in1({8{1'b1}}), .out(multiplexer_3_out), .sel(or_2_out));
  displayTime displaytime_2 (.in_1(counter_1_out_10), .out_2(displaytime_2_out_2));
  Multiplexer #(.width(8), .enable("false")) multiplexer_4 (
    .in0(multiplexer_1_out), .in1({8{1'b1}}), .out(multiplexer_4_out), .sel(comparator_1_gt));
  Register #(.width(4)) an (.D(multiplexer_2_out), .en(clock_2_out_5));  // open: Q, clk, clr
  displayTime displaytime_3 (.in_1(counter_1_out_9), .out_2(displaytime_3_out_2));
  Multiplexer #(.width(8), .enable("false")) multiplexer_5 (
    .in0(multiplexer_4_out), .in1(multiplexer_3_out), .out(multiplexer_5_out), .sel(undriven_4));
  displayTime displaytime_4 (.in_1(counter_1_out_8), .out_2(displaytime_4_out_2));
  Multiplexer #(.width(8), .enable("false")) multiplexer_6 (
    .in0(multiplexer_1_out), .in1(multiplexer_5_out), .out(multiplexer_6_out), .sel(undriven_5));
  Register seg (.D(multiplexer_6_out), .en(clock_2_out_5));  // open: Q, clk, clr

  // Notes on the sheet:
  //   rst
  //   reset_debounce
  //   clock_mod
  //   adj
  //   sel
  //   pause
  //   pause_debounce
  //   counter_mod
  //   display_min10
  //   display_min1
  //   display_sec10
  //   adj
  //   sel
  //   display_sec1
endmodule

module Clock (
  input  in_1,
  input  in_2,
  output out_3,
  output out_4,
  output out_5,
  output out_6
);
endmodule

module Debouncer (
  input  in_1,
  input  in_2,
  output out_3
);
endmodule

module Counter (
  input  in_1,
  input  in_2,
  input  in_3,
  input  in_4,
  input  in_5,
  input  in_6,
  input  in_7,
  output [3:0] out_8,
  output [3:0] out_9,
  output [3:0] out_10,
  output [3:0] out_11
);
endmodule

module displayTime (
  input  [3:0] in_1,
  output [7:0] out_2
);
endmodule
