// Logisim project div_factor.circ as structural Verilog: 1 circuit, main circuit main
module main (
);

  wire [3:0] undriven;
  wire [25:0] multiplexer_1_out;

  Multiplexer #(.select(4), .width(26), .enable("false")) multiplexer_1 (
    .in0(26'h14fb180), .in1(26'h243d580), .in2(26'h2255100), .in3(26'h206cc80), .in4(26'h1e84800),
    .in5(26'h1c9c380), .in6(26'h1ab3f00), .in7(26'h18cba80), .in8(26'h16e3600), .in9(26'h14fb180),
    .in10(26'h14fb180), .in11(26'h14fb180), .in12(26'h14fb180), .in13(26'h14fb180), .in14(26'h14fb180),
    .in15(26'h14fb180), .out(multiplexer_1_out), .sel(undriven));

  // Notes on the sheet:
  //   curr_level
  //   div_factor
endmodule
