// Logisim project move_clk.circ as structural Verilog: 1 circuit, main circuit main
module main (
);

  wire clock_1_out, clock_2_out, comparator_1_eq, multiplexer_2_out, multiplexer_4_out, not_1_out, tempclk_q,
       undriven_2, undriven_3, undriven_4, undriven_5, undriven_6;
  wire [31:0] adder_1_out, cnt_q, multiplexer_1_out, multiplexer_3_out, subtractor_1_out, undriven;

  Adder #(.width(32)) adder_1 (.a(cnt_q), .b(32'h1), .out(adder_1_out));  // open: cin, cout
  Subtractor #(.width(32)) subtractor_1 (.a(undriven), .b(32'h1), .out(subtractor_1_out));  // open: bin, bout
  Multiplexer #(.width(32), .enable("false")) multiplexer_1 (
    .in0(adder_1_out), .in1({32{1'b0}}), .out(multiplexer_1_out), .sel(comparator_1_eq));
  Comparator #(.width(32)) comparator_1 (.a(cnt_q), .b(subtractor_1_out), .eq(comparator_1_eq));  // open: gt, lt
  not not_1 (not_1_out, undriven_2);
  Multiplexer #(.enable("false")) multiplexer_2 (
    .in0(undriven_2), .in1(not_1_out), .out(multiplexer_2_out), .sel(comparator_1_eq));
  Multiplexer #(.width(32), .enable("false")) multiplexer_3 (
    .in0(multiplexer_1_out), .in1({32{1'b0}}), .out(multiplexer_3_out), .sel(undriven_3));
  Multiplexer #(.enable("false")) multiplexer_4 (
    .in0(multiplexer_2_out), .in1(1'b0), .out(multiplexer_4_out), .sel(undriven_4));
  Clock clock_1 (.out(clock_1_out));
  Clock clock_2 (.out(clock_2_out));
  Register #(.width(32)) cnt (.D(multiplexer_3_out), .en(clock_1_out), .Q(cnt_q), .clr(undriven_5));  // open: clk
  Register #(.width(1)) tempclk (
    .D(multiplexer_4_out), .en(clock_2_out), .Q(tempclk_q), .clr(undriven_6));  // open: clk

  // Notes on the sheet:
  //   x
  //   tempclk
  //   rst
  //   rst
  //   rst
  //   move
  //   rst
endmodule
